# Fritzing sketch HaterMatic_Diagram (saved by Fritzing 0.8.7b)
breadboards: 1

parts:
  Part1 = Coin Acceptor - 6-Coin version
  Part2 = Arduino Pro Mini v13
  Part3 = Thermal Printer
  Power_plug1 = Power plug
  Power_plug2 = Power plug
  S1 = Arcade Button

nets:
  N1: Part1.INH, Part2.D9_PWM
  GND: Part1.GND, Part2.GND, Part3.GND#2, Power_plug1.SW, S1.COM
  N2: Part1.SIG, Part2.D7
  12V: Part1.12V, Part2.RAW, Power_plug1.VCC
  N3: Part2.A0, S1.NO
  N4: Part2.D8, Part3.RXD
  N5: Part3.GND#0, Power_plug2.SW
  N6: Part3.VH, Power_plug2.VCC

notes:
  9V supply
  connection
  12V supply
  connection

custom parts:
  Coin Acceptor - 6-Coin version: 12V coin acceptor that can handle up to 6 different denominations. Output is either pulse width, serial, or single pin per coin value.
  Power plug: Power input plug for 5.0x2.1mm barrel plugs. Mates to most power supplies sold by SparkFun.
  Arcade Button: Standard arcade button, SPDT
